# Fritzing sketch ProjectACircuitDiagram (saved by Fritzing 0.9.3b)
breadboards: 3

parts:
  Raspberry_Pi_1 = Raspberry Pi 3 [part_number=RPI-3-V1.2]
  ADC1 = MCP3008 [package=dil16]
  T1 = TMP36 Temperature Sensor [package="TO92 [THT]"]
  U4 = MCP7384XX [package=msop8]
  Y2 = CRYSTAL [package=crystal-32khz-smd_epson_mc146]
  C3 = Ceramic Capacitor [capacitance=100nF package="100 mil [THT, multilayer]"]
  C4 = Ceramic Capacitor [capacitance=100nF package="100 mil [THT, multilayer]"]
  U5 = MCP41xxx [package=so08]
  S3 = Pushbutton [package="[THT]"]
  S4 = Pushbutton [package="[THT]"]
  R1 = TRIMPOT [package=trimpot_pth_s3_lock]
  R2 = Photocell (LDR) [package=THT]
  R3 = Resistor [tolerance=±5% resistance=220 package=THT]
  S5 = Pushbutton [package="[THT]"]
  S6 = Pushbutton [package="[THT]"]

nets:
  3V3: Raspberry_Pi_1.3v3, ADC1.VREF, ADC1.VDD, U4.DRV, U5.CS, U5.W, R1.CCW, R3.Pin_1
  N1: Raspberry_Pi_1.GPIO2, U4.TIMER
  N2: Raspberry_Pi_1.GPIO3, U4.VSS
  N3: Raspberry_Pi_1.GPIO4, S6.Pin_3, S6.Pin_4
  N4: Raspberry_Pi_1.GPIO17, S3.Pin_3, S3.Pin_4
  N5: Raspberry_Pi_1.GPIO27, S4.Pin_3, S4.Pin_4
  N6: Raspberry_Pi_1.GPIO22, S5.Pin_3, S5.Pin_4
  N7: Raspberry_Pi_1.GPIO10, ADC1.Din, U5.GND
  N8: Raspberry_Pi_1.GPIO9, ADC1.Dout
  N9: Raspberry_Pi_1.GPIO11, ADC1.CLK, U5.DI
  N10: Raspberry_Pi_1.GPIO8, ADC1.CS/SHDN, U5.SCK
  GND: Raspberry_Pi_1.GND, ADC1.DGND, ADC1.AGND, T1.GND, U4.EN, C3.0, C4.1, U5.A, U5.B, S3.Pin_1, S3.Pin_2, S4.Pin_1, S4.Pin_2, R1.CW, R2.pin_1, S5.Pin_1, S5.Pin_2, S6.Pin_1, S6.Pin_2
  N11: Raspberry_Pi_1.5V, T1.+Vs
  N12: ADC1.CH0, R1.WIPER
  N13: ADC1.CH1, T1.Vout
  N14: ADC1.CH7, R2.pin_0, R3.Pin_0
  N15: U4.SENSE, Y2.2, C3.1
  N16: U4.VDD, Y2.1, C4.0

notes:
  Vdd/Vcc
  VREF
  AGND
  CLK
  DOUT
  CS'/SHDN
  DIN
  DGND
  VDD
  CH0
  CH7
  CH1
  CH2
  CH5
  CH3
  CH4
  CH6
  10kΩ
  RESET
  FREQ
  STOP
  DISMISS

// code stored in the sketch: Blink.ino
/*=====================================================================
  This program is free software: you can redistribute it and/or modify
  it under the terms of the GNU General Public License as published by
  the Free Software Foundation, either version 3 of the License, or
  (at your option) any later version.

  This program is distributed in the hope that it will be useful,
  but WITHOUT ANY WARRANTY; without even the implied warranty of
  MERCHANTABILITY or FITNESS FOR A PARTICULAR PURPOSE.  See the
  GNU General Public License for more details.

  You should have received a copy of the GNU General Public License
  along with this program.  If not, see <http://www.gnu.org/licenses/>.
  ---------------------------------------------------------------------
  Purpose : Blink two LEDs alternatively.
  Date    : 21 Nov 2015
  Boards  : ArduinoUno, LaunchPadF5529
  =====================================================================
*/

// Comment/uncomment as suitable for your hardware
// #define LaunchPadF5529

#ifdef LaunchPadF5529
#define LED1 RED_LED // on-board, aka P1_0
#define LED2 GREEN_LED // on-board, aka P4_7
#else
#define LED1 13 // on-board
#define LED2 2 // external
#endif

void setup() {                
  pinMode(LED1, OUTPUT);
  pinMode(LED2, OUTPUT);
}

void loop() {
  digitalWrite(LED1, HIGH);
  digitalWrite(LED2, LOW);
  delay(1000);

  digitalWrite(LED1, LOW);
  digitalWrite(LED2, HIGH);
  delay(1000);
}

// code stored in the sketch: sss.ino
/*=====================================================================
  This program is free software: you can redistribute it and/or modify
  it under the terms of the GNU General Public License as published by
  the Free Software Foundation, either version 3 of the License, or
  (at your option) any later version.

  This program is distributed in the hope that it will be useful,
  but WITHOUT ANY WARRANTY; without even the implied warranty of
  MERCHANTABILITY or FITNESS FOR A PARTICULAR PURPOSE.  See the
  GNU General Public License for more details.

  You should have received a copy of the GNU General Public License
  along with this program.  If not, see <http://www.gnu.org/licenses/>.
  ---------------------------------------------------------------------
  Purpose : Blink two LEDs alternatively.
  Date    : 21 Nov 2015
  Board   : ArduinoUno, LaunchPadF5529
  =====================================================================
*/

// Comment/uncomment as suitable to your hardware
// #define LaunchPadF5529

#ifdef LaunchPadF5529
#define LED1 RED_LED // on-board, aka P1_0
#define LED2 GREEN_LED // on-board, aka P4_7
#else
#define LED1 13 // on-board
#define LED2 2 // external
#endif

void setup() {                
  pinMode(LED1, OUTPUT);
  pinMode(LED2, OUTPUT);
}

void loop() {
  digitalWrite(LED1, HIGH);
  digitalWrite(LED2, LOW);
  delay(1000);

  digitalWrite(LED1, LOW);
  digitalWrite(LED2, HIGH);
  delay(1000);
}
